# Fritzing sketch LT8330 StepUp PCB (saved by Fritzing 0.9.3b)
breadboards: 1

parts:
  R1 = Resistor [tolerance=±5% resistance=1M package=THT]
  C2 = Ceramic Capacitor [capacitance=1µF voltage=50V package="100 mil [THT, multilayer]"]
  D1 = Diode [part_number=PMEG6010CEJ package=sod-323]
  C4 = Ceramic Capacitor [capacitance=100nF part_number=SR201C104KAR package="100 mil [THT, multilayer]"]
  J2 = female pin header, 2 pins [form="♀ (female)" part_number="Output Power"]
  J1 = female pin header, 2 pins [form="♀ (female)"]
  J1_2 = female pin header, 2 pins [form="♀ (female)" part_number="Input Power"]
  J3 = female pin header, 3 pins [form="♀ (female)" part_number="Audio In 48V Phantom"]
  J4 = female pin header, 3 pins [form="♀ (female)" part_number="Audio Out"]
  J5 = female pin header, 2 pins [form="♀ (female)" part_number="Output Power"]
  R3 = Resistor [tolerance=±5% resistance=1M package=THT]
  R4 = Resistor [tolerance=±5% resistance=1M package=THT]
  R5 = Resistor [tolerance=±5% resistance=6.8k package=THT]
  R6 = Resistor [tolerance=±5% resistance=6.8k package=THT]
  C5 = Ceramic Capacitor [capacitance=1µF voltage=0.1kV part_number=C340C105K1R5TA package="200 mil [THT, multilayer]"]
  C6 = Ceramic Capacitor [capacitance=1µF voltage=0.1kV part_number=C340C105K1R5TA package="200 mil [THT, multilayer]"]
  C9 = Capacitor [part_number="80V, 4.7uF, GRM32ER71K475KE14L" package=1210]
  C10 = Capacitor [part_number="80V, 4.7uF, GRM32ER71K475KE14L" package=1210]
  L1 = Inductor [inductance=680nH part_number=B78108E1681M000 package="400 mil [THT]"]
  U1 = LT8330 [package=SOT23-6]
  R2 = Resistor [tolerance=±5% resistance=34.8k package=THT]
  J6 = female pin header, 2 pins [form="♀ (female)" part_number="Input Power"]
  U2 = 3.5mm Audio Jack [package=audio-jack]

nets:
  N1: R1.Pin_0, U1.FBX, R2.Pin_1
  N2: R1.Pin_1, D1.C, C4.1, J2.pin1, J5.pin1, R5.Pin_0, R6.Pin_0, C9.1
  GND: C2.0, C4.0, J2.pin2, J1.pin2, J1_2.pin2, J3.pin3, J4.pin3, J5.pin2, R3.Pin_0, R4.Pin_0, C9.2, C10.2, U1.GND, R2.Pin_0, J6.pin2, U2.SLEEVE
  N3: C2.1, U1.INTVCC
  N4: D1.A, L1.pin_0, U1.SW
  N5: J1_2.pin1, C10.1, L1.pin_1, U1.EN, U1.VIN, J6.pin1
  N6: J3.pin1, R6.Pin_1, C6.1
  N7: J3.pin2, R5.Pin_1, C5.1
  N8: J4.pin1, R3.Pin_1, C5.0, U2.LEFT
  N9: J4.pin2, R4.Pin_1, C6.0, U2.RIGHT

custom parts:
  LT8330: The LT®8330 is a current mode DC/DC converter capable of generating either positive or negative output voltages using a single feedback pin.
